// Logisim project Lab6.circ as structural Verilog: 3 circuits, main circuit main
module main (
  input  A,
  input  B,
  input  C,
  output Sum,
  output C_out
);

  wire and_1_out, and_2_out, and_3_out, and_4_out, and_5_out, and_6_out, and_7_out, and_8_out, and_9_out,
       and_10_out, and_11_out, not_1_out, not_2_out, not_3_out, or_1_out, or_2_out, or_3_out;

  not not_1 (not_1_out, A);
  not not_2 (not_2_out, B);
  not not_3 (not_3_out, C);
  and and_1 (and_1_out, not_1_out, not_2_out);
  and and_2 (and_2_out, not_1_out, B);
  and and_3 (and_3_out, A, not_2_out);
  and and_4 (and_4_out, A, B);
  and and_5 (and_5_out, and_1_out, C);
  and and_6 (and_6_out, and_2_out, not_3_out);
  and and_7 (and_7_out, and_3_out, not_3_out);
  and and_8 (and_8_out, and_4_out, C);
  and and_9 (and_9_out, C, A);
  and and_10 (and_10_out, C, B);
  and and_11 (and_11_out, B, A);
  or or_1 (or_1_out, and_5_out, and_6_out);
  or or_2 (or_2_out, and_7_out, and_8_out);
  or or_3 (or_3_out, and_9_out, and_10_out);
  or or_4 (Sum, or_1_out, or_2_out);
  or or_5 (C_out, or_3_out, and_11_out);
endmodule

module _4_Bit_adder (
  input  [3:0] in_1,
  input  [3:0] in_2,
  output [3:0] out_3
);

  wire main_1_c_out, main_3_c_out, main_4_c_out;

  main main_1 (.A(in_2[2]), .B(in_1[2]), .C(main_3_c_out), .Sum(out_3[2]), .C_out(main_1_c_out));
  main main_2 (.A(in_2[3]), .B(in_1[3]), .C(main_1_c_out), .Sum(out_3[3]));  // open: C_out
  main main_3 (.A(in_2[1]), .B(in_1[1]), .C(main_4_c_out), .Sum(out_3[1]), .C_out(main_3_c_out));
  main main_4 (.A(in_2[0]), .B(in_1[0]), .C(1'b0), .Sum(out_3[0]), .C_out(main_4_c_out));
endmodule

module adder_subtract (
  input  [7:0] in_1,
  input  [7:0] in_2,
  input  in_3,
  output [7:0] out_4
);

  wire [7:0] adder_1_out, subtractor_1_out;

  Adder adder_1 (.a(in_1), .b(in_2), .out(adder_1_out), .cin(1'b0));  // open: cout
  Subtractor subtractor_1 (.a(in_1), .b(in_2), .out(subtractor_1_out), .bin(1'b0));  // open: bout
  Multiplexer #(.width(8)) multiplexer_1 (
    .in0(adder_1_out), .in1(subtractor_1_out), .out(out_4), .sel(in_3));  // open: en
endmodule
