// Logisim project Project-4 Full CPU Circuit.circ as structural Verilog: 3 circuits, main circuit main
module main (
  input  [15:0] Operand_1__Multiplicand_or_Dividend,
  input  [15:0] Operand_2__Multiplier_and_Divisor,
  input  Mul,
  input  Div,
  output [31:0] Product,
  output M_Ready,
  output [15:0] Quotient,
  output [15:0] Remainder,
  output D_Ready_DIVISON_ONLY_WORKS_IF_RUN_EXACTLY_18_TIMES
);

  wire Clock_out;

  _16_bit_Division u_16_bit_division_1 (
    .Dividend(Operand_1__Multiplicand_or_Dividend), .Divisor(Operand_2__Multiplier_and_Divisor), .Div(Div),
    .Clock(Clock_out), .Quotient(Quotient), .Remainder(Remainder),
    .D_Ready(D_Ready_DIVISON_ONLY_WORKS_IF_RUN_EXACTLY_18_TIMES));
  Clock Clock (.out(Clock_out));
  _16_bit_Multiplication u_16_bit_multiplication_1 (
    .Multiplicand(Operand_1__Multiplicand_or_Dividend), .Multiplier(Operand_2__Multiplier_and_Divisor),
    .Mul(Mul), .Clock(Clock_out), .Product(Product), .M_Ready(M_Ready));
endmodule

module _16_bit_Multiplication (
  input  [15:0] Multiplicand,
  input  [15:0] Multiplier,
  input  Mul,
  input  Clock,
  output [31:0] Product,
  output M_Ready
);

  wire and_1_out, not_1_out;
  wire [7:0] counter_1_q, rom_1_data;
  wire [15:0] multiplexer_1_out, multiplier_register_q, shifter_1_out;
  wire [31:0] adder_1_out, bit_extender_1_out, multiplexer_2_out, multiplexer_3_out, multiplexer_4_out,
       multiplicand_q, shifter_2_out;

  Multiplexer #(.width(16)) multiplexer_1 (
    .in0(shifter_1_out), .in1(Multiplier), .out(multiplexer_1_out), .sel(rom_1_data[0]));  // open: en
  Counter #(.max('h10), .ongoal("stay")) counter_1 (
    .Q(counter_1_q), .carry(M_Ready), .clk(and_1_out), .clr(not_1_out));  // open: load, D, count
  not not_1 (not_1_out, Mul);
  and and_1 (and_1_out, Mul, Clock);
  assign bit_extender_1_out = {{16{Multiplicand[15]}}, Multiplicand};  // Bit_Extender bit_extender_1
  Shifter #(.width(16), .shift("lr")) shifter_1 (.in(multiplier_register_q), .\dist (4'b0001), .out(shifter_1_out));
  Register #(.width(16)) multiplier_register (
    .D(multiplexer_1_out), .Q(multiplier_register_q), .clk(and_1_out));  // open: en, clr
  ROM rom_1 (.addr(counter_1_q), .data(rom_1_data));  // open: sel
  Multiplexer #(.width(32)) multiplexer_2 (
    .in0(shifter_2_out), .in1(bit_extender_1_out), .out(multiplexer_2_out), .sel(rom_1_data[0]));  // open: en
  Register #(.width(32)) u_multiplicand (.D(multiplexer_2_out), .Q(multiplicand_q), .clk(and_1_out));  // open: en, clr
  Shifter #(.width(32)) shifter_2 (.in(multiplicand_q), .\dist (5'b00001), .out(shifter_2_out));
  Multiplexer #(.width(32)) multiplexer_3 (
    .in0({32{1'b0}}), .in1(multiplicand_q), .out(multiplexer_3_out), .sel(multiplier_register_q[0]));  // open: en
  Adder #(.width(32)) adder_1 (.a(Product), .b(multiplexer_3_out), .out(adder_1_out));  // open: cin, cout
  Multiplexer #(.width(32)) multiplexer_4 (
    .in0(adder_1_out), .in1({32{1'b0}}), .out(multiplexer_4_out), .sel(rom_1_data[0]));  // open: en
  Register #(.width(32)) u_product (.D(multiplexer_4_out), .Q(Product), .clk(and_1_out));  // open: en, clr

  // Notes on the sheet:
  //   contents of rom_1 (hex, n*v repeats v):
  //   1
  //   Clock to Registers
endmodule

module _16_bit_Division (
  input  [15:0] Dividend,
  input  [15:0] Divisor,
  input  Div,
  input  Clock,
  output [15:0] Quotient,
  output [15:0] Remainder,
  output D_Ready
);

  wire and_1_out, comparator_1_eq, comparator_1_gt, comparator_1_lt, comparator_2_eq, not_1_out, or_1_out;
  wire [7:0] counter_1_q, rom_1_data;
  wire [15:0] adder_2_out, multiplexer_4_out, multiplexer_5_out, Quotient_q, shifter_2_out;
  wire [31:0] adder_1_out, bit_extender_1_out, Divosor_q, multiplexer_1_out, multiplexer_2_out,
       multiplexer_3_out, Remainder_q, shifter_1_out, subtractor_1_out;
  wire [31:16] multiplexer_7_out;

  assign bit_extender_1_out = {{16{1'b0}}, Dividend};  // Bit_Extender bit_extender_1
  ROM rom_1 (.addr(counter_1_q), .data(rom_1_data));  // open: sel
  Counter #(.max('h12), .ongoal("stay")) counter_1 (
    .Q(counter_1_q), .carry(D_Ready), .clk(and_1_out), .clr(not_1_out));  // open: load, D, count
  not not_1 (not_1_out, Div);
  and and_1 (and_1_out, Div, Clock);
  Shifter #(.width(32), .shift("lr")) shifter_1 (.in(Divosor_q), .\dist (5'b00001), .out(shifter_1_out));
  Register #(.width(32)) Divosor (.D(multiplexer_1_out), .Q(Divosor_q), .clk(and_1_out));  // open: en, clr
  Multiplexer #(.width(32)) multiplexer_1 (
    .in0(shifter_1_out), .in1({Divisor, {16{1'b0}}}), .out(multiplexer_1_out), .sel(rom_1_data[0]));  // open: en
  Multiplexer #(.width(32)) multiplexer_2 (
    .in0(multiplexer_3_out), .in1(bit_extender_1_out), .out(multiplexer_2_out), .sel(rom_1_data[0]));  // open: en
  Subtractor #(.width(32)) subtractor_1 (.a(Remainder_q), .b(Divosor_q), .out(subtractor_1_out));  // open: bin, bout
  Adder #(.width(32)) adder_1 (.a(subtractor_1_out), .b(Divosor_q), .out(adder_1_out));  // open: cin, cout
  Register #(.width(32)) u_Remainder (.D(multiplexer_2_out), .Q(Remainder_q), .clk(and_1_out));  // open: en, clr
  Comparator #(.width(32)) comparator_1 (
    .a(subtractor_1_out), .b({32{1'b0}}), .gt(comparator_1_gt), .eq(comparator_1_eq), .lt(comparator_1_lt));
  or or_1 (or_1_out, comparator_1_gt, comparator_1_eq);
  Multiplexer #(.width(32)) multiplexer_3 (
    .in0(subtractor_1_out), .in1(adder_1_out), .out(multiplexer_3_out), .sel(comparator_1_lt));  // open: en
  Multiplexer #(.width(16)) multiplexer_4 (
    .in0(shifter_2_out), .in1(adder_2_out), .out(multiplexer_4_out), .sel(or_1_out));  // open: en
  Comparator #(.width(32), .mode("unsigned")) comparator_2 (
    .a(bit_extender_1_out), .b({Divisor, {16{1'b0}}}), .eq(comparator_2_eq));  // open: gt, lt
  Adder #(.width(16)) adder_2 (.a(shifter_2_out), .b(16'h1), .out(adder_2_out));  // open: cin, cout
  Register #(.width(16)) u_Quotient (.D(multiplexer_5_out), .Q(Quotient_q), .clk(and_1_out));  // open: en, clr
  Multiplexer #(.width(16)) multiplexer_5 (
    .in0(multiplexer_4_out), .in1({16{1'b0}}), .out(multiplexer_5_out), .sel(rom_1_data[0]));  // open: en
  Shifter #(.width(16)) shifter_2 (.in(Quotient_q), .\dist (4'b0001), .out(shifter_2_out));
  Multiplexer #(.width(16)) multiplexer_6 (
    .in0(Quotient_q), .in1(16'h1), .out(Quotient), .sel(comparator_2_eq));  // open: en
  Multiplexer #(.width(32)) multiplexer_7 (
    .in0(Remainder_q), .in1({32{1'b0}}), .out({multiplexer_7_out, Remainder}), .sel(comparator_2_eq));  // open: en

  // Notes on the sheet:
  //   contents of rom_1 (hex, n*v repeats v):
  //   1
  //   Clock to Registers
endmodule
